# Fritzing sketch fritzing (saved by Fritzing 0.9.3b)
breadboards: 1

parts:
  U1 = ESP32S-HiLetgo [part_number=ESP32S-HiLetgo]
  hc-sr1 = hc-sr04
  electronicsguy1 = electronicsguy 0.96" 128x64 SPI I2C OLED

nets:
  GND: U1.GND, hc-sr1.GND, electronicsguy1.GND
  VCC: U1.VIN, hc-sr1.VCC, electronicsguy1.VCC
  N1: U1.GPIO15, hc-sr1.Echo
  N2: U1.GPIO2, hc-sr1.Trig
  N3: U1.GPIO16, electronicsguy1.DC
  N4: U1.GPIO17, electronicsguy1.RES
  N5: U1.GPIO18, electronicsguy1.SCL
  N6: U1.GPIO23, electronicsguy1.SDA

custom parts:
  ESP32S-HiLetgo: HiLetgo ESP-WROOM-32 ESP32 ESP-32S Development Board 2.4GHz Dual-Mode WiFi + Bluetooth Dual Cores Microcontroller The ESP32 integrated with Antenna switches, RF Balun, power amplifiers, low-noise amplifiers, filters, and management modules, and the entire solution occupies the least area of PCB. 2.4 GHz Wi-Fi plus Bluetooth dual-mode chip, with TSMC Ultra-low power consumption 40nm technology,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
  electronicsguy 0.96" 128x64 SPI I2C OLED: Generic 0.96" 128x64 SPI I2C OLED Default is SPI mode Can be re-configured for I2C (needs soldering work) Comes in various colors like blue, white, yellow-blue
